// Logisim project simpleRISC_reduced.circ as structural Verilog: 5 circuits, main circuit main
module main (
);

  wire add, CLK, cmp, flag_eq, flag_gt, I, is_eq, is_gt, RegWEn, sub;
  wire [3:0] ALUsel;
  wire [31:0] adder_1_out, Immediate_32_bit, INSTRUCTION, operand2_val, PC, REG_W_DATA, rs1_data, rs2_data,
       signed_extend, unsigned_extend, up_shifted;

  Clock clock_1 (.out(CLK));
  Comparator #(.width(5)) comparator_1 (.a(INSTRUCTION[31:27]), .b(5'b00001), .gt(cmp), .eq(sub), .lt(add));
  Register #(.width(32)) register_1 (.D(adder_1_out), .en(CLK), .clk(CLK), .Q(PC));  // open: clr
  Adder #(.width(32)) adder_1 (.a(PC), .b(32'h4), .out(adder_1_out));  // open: cin, cout
  LED led_1 (.in(cmp));
  LED led_2 (.in(RegWEn));
  LED led_3 (.in(flag_eq));
  LED led_4 (.in(flag_gt));
  or or_1 (RegWEn, add, sub);
  // LedBar #(.inputtype("row"), .matrixcols(32)) ledbar_1: pin names not known; wires that end beside it: 32'h4, REG_W_DATA
  IMEM imem_1 (.IMEM_ADDR(PC), .INSTRUCTION({INSTRUCTION[31:27], I, INSTRUCTION[25:0]}));
  ALU alu_1 (
    .ALU_X(rs1_data), .ALU_Y(operand2_val), .ALU_OP(ALUsel), .ALU_RESULT(REG_W_DATA), .ALU_IS_EQ(is_eq),
    .ALU_IS_GT(is_gt));
  Multiplexer #(.select(2), .width(4)) multiplexer_1 (
    .in1(4'b0000), .in2(4'b0001), .out(ALUsel), .sel({sub, add}));  // open: in0, in3
  assign signed_extend = {{16{INSTRUCTION[15]}}, INSTRUCTION[15:0]};  // Bit_Extender bit_extender_1
  assign unsigned_extend = {{16{1'b0}}, INSTRUCTION[15:0]};  // Bit_Extender bit_extender_2
  Multiplexer #(.select(2), .width(32)) multiplexer_2 (
    .in0(signed_extend), .in2(unsigned_extend), .in3(up_shifted), .out(Immediate_32_bit),
    .sel(INSTRUCTION[17:16]));  // open: in1
  LedBar #(.matrixcols(32)) ledbar_2 (
    .led0(INSTRUCTION[31]), .led1(INSTRUCTION[30]), .led2(INSTRUCTION[29]), .led3(INSTRUCTION[28]),
    .led4(INSTRUCTION[27]), .led5(I), .led6(INSTRUCTION[25]), .led7(INSTRUCTION[24]), .led8(INSTRUCTION[23]),
    .led9(INSTRUCTION[22]), .led10(INSTRUCTION[21]), .led11(INSTRUCTION[20]), .led12(INSTRUCTION[19]),
    .led13(INSTRUCTION[18]), .led14(INSTRUCTION[17]), .led15(INSTRUCTION[16]), .led16(INSTRUCTION[15]),
    .led17(INSTRUCTION[14]), .led18(INSTRUCTION[13]), .led19(INSTRUCTION[12]), .led20(INSTRUCTION[11]),
    .led21(INSTRUCTION[10]), .led22(INSTRUCTION[9]), .led23(INSTRUCTION[8]), .led24(INSTRUCTION[7]),
    .led25(INSTRUCTION[6]), .led26(INSTRUCTION[5]), .led27(INSTRUCTION[4]), .led28(INSTRUCTION[3]),
    .led29(INSTRUCTION[2]), .led30(INSTRUCTION[1]), .led31(INSTRUCTION[0]));
  REGFILE regfile_1 (
    .rs1(INSTRUCTION[21:18]), .rs2(INSTRUCTION[17:14]), .rd(INSTRUCTION[25:22]), .REG_W_DATA(REG_W_DATA),
    .WRITE_EN(RegWEn), .CLK(CLK), .rs1_data(rs1_data), .rs2_data(rs2_data));
  Shifter #(.width(32)) shifter_1 (.in(unsigned_extend), .\dist (5'b10000), .out(up_shifted));
  LedBar #(.matrixcols(32)) ledbar_3 (
    .led0(rs1_data[31]), .led1(rs1_data[30]), .led2(rs1_data[29]), .led3(rs1_data[28]), .led4(rs1_data[27]),
    .led5(rs1_data[26]), .led6(rs1_data[25]), .led7(rs1_data[24]), .led8(rs1_data[23]), .led9(rs1_data[22]),
    .led10(rs1_data[21]), .led11(rs1_data[20]), .led12(rs1_data[19]), .led13(rs1_data[18]),
    .led14(rs1_data[17]), .led15(rs1_data[16]), .led16(rs1_data[15]), .led17(rs1_data[14]),
    .led18(rs1_data[13]), .led19(rs1_data[12]), .led20(rs1_data[11]), .led21(rs1_data[10]),
    .led22(rs1_data[9]), .led23(rs1_data[8]), .led24(rs1_data[7]), .led25(rs1_data[6]), .led26(rs1_data[5]),
    .led27(rs1_data[4]), .led28(rs1_data[3]), .led29(rs1_data[2]), .led30(rs1_data[1]), .led31(rs1_data[0]));
  LedBar #(.matrixcols(32)) ledbar_4 (
    .led0(rs2_data[31]), .led1(rs2_data[30]), .led2(rs2_data[29]), .led3(rs2_data[28]), .led4(rs2_data[27]),
    .led5(rs2_data[26]), .led6(rs2_data[25]), .led7(rs2_data[24]), .led8(rs2_data[23]), .led9(rs2_data[22]),
    .led10(rs2_data[21]), .led11(rs2_data[20]), .led12(rs2_data[19]), .led13(rs2_data[18]),
    .led14(rs2_data[17]), .led15(rs2_data[16]), .led16(rs2_data[15]), .led17(rs2_data[14]),
    .led18(rs2_data[13]), .led19(rs2_data[12]), .led20(rs2_data[11]), .led21(rs2_data[10]),
    .led22(rs2_data[9]), .led23(rs2_data[8]), .led24(rs2_data[7]), .led25(rs2_data[6]), .led26(rs2_data[5]),
    .led27(rs2_data[4]), .led28(rs2_data[3]), .led29(rs2_data[2]), .led30(rs2_data[1]), .led31(rs2_data[0]));
  Register #(.width(1)) u_flag_eq (.D(is_eq), .en(cmp), .clk(CLK), .Q(flag_eq));  // open: clr
  Register #(.width(1)) u_flag_gt (.D(is_gt), .en(cmp), .clk(CLK), .Q(flag_gt));  // open: clr
  Multiplexer #(.width(32)) multiplexer_3 (.in0(rs2_data), .in1(Immediate_32_bit), .out(operand2_val), .sel(I));

  // Other names for the same wires on the sheet: num_16_bit[15:0] = INSTRUCTION[15:0]; rs2[3:0] = INSTRUCTION[17:14];
  //   modifier[1:0] = INSTRUCTION[17:16]; rs1[3:0] = INSTRUCTION[21:18]; rd[3:0] = INSTRUCTION[25:22];
  //   INSTRUCTION[26] = I; OP[4:0] = INSTRUCTION[31:27]
endmodule

module DMEM (
  input  [31:0] DMEM_ADDR,
  input  DMEM_W_EN,
  input  CLK,
  input  [31:0] DMEM_W_DATA,
  output [31:0] DMEM_R_DATA
);

  RAM #(.addrWidth(10), .dataWidth(32), .enables("line")) ram_1 (
    .addr(DMEM_ADDR[9:0]), .we(DMEM_W_EN), .clk(CLK), .din(DMEM_W_DATA), .dout(DMEM_R_DATA));

  // Other names for the same wires on the sheet: DMEM_READ_DATA[31:0] = DMEM_R_DATA;
  //   DMEM_WRITE_DATA[31:0] = DMEM_W_DATA; DMEM_WRITE_EN = DMEM_W_EN
endmodule

module IMEM (
  input  [31:0] IMEM_ADDR,
  output [31:0] INSTRUCTION
);

  wire rom_1_p2;

  // ROM #(.addrWidth(10), .line("quad")) rom_1: pin names not known; wires that end beside it: IMEM_ADDR[9:0], rom_1_p2, INSTRUCTION[7:0], INSTRUCTION[15:8], INSTRUCTION[23:16], INSTRUCTION[31:24]

  // Notes on the sheet:
  //   contents of rom_1 (hex, n*v repeats v):
  //   f 0 dc 5 10 0 30 7 0 0 7 1 0 0 31 3 11 0 30 d 64 0 44 c 14 0 44 4 0 0 7 28 b0 ff 64 6 0 40 6 28 0 0
  //   e7 a 0 c0 26 28 9d ff 9a 5 3f 0 cf 4 ff 9d 19 28 0 c0 58 1 0 80 15 28 5*0 40 19 28
endmodule

module REGFILE (
  input  [3:0] rs1,
  input  [3:0] rs2,
  input  [3:0] rd,
  input  [31:0] REG_W_DATA,
  input  WRITE_EN,
  input  CLK,
  output [31:0] rs1_data,
  output [31:0] rs2_data
);

  wire WE_1, WE_2, WE_3, WE_4, WE_5, WE_6, WE_7, WE_8, WE_9, WE_10, WE_11, WE_12, WE_13, WE_14, WE_15, WE_16,
       WE_17, WE_18, WE_19, WE_20, WE_21, WE_22, WE_23, WE_24, WE_25, WE_26, WE_27, WE_28, WE_29, WE_30,
       WE_31;
  wire [31:0] in_r1, in_r2, in_r3, in_r4, in_r5, in_r6, in_r7, in_r8, in_r9, in_r10, in_r11, in_r12, in_r13,
       in_r14, in_r15, in_r16, in_r17, in_r18, in_r19, in_r20, in_r21, in_r22, in_r23, in_r24, in_r25,
       in_r26, in_r27, in_r28, in_r29, in_r30, in_r31, out_r1, out_r2, out_r3, out_r4, out_r5, out_r6,
       out_r7, out_r8, out_r9, out_r10, out_r11, out_r12, out_r13, out_r14, out_r15, out_r16, out_r17,
       out_r18, out_r19, out_r20, out_r21, out_r22, out_r23, out_r24, out_r25, out_r26, out_r27, out_r28,
       out_r29, out_r30, out_r31;

  Register #(.width(32)) r1 (.D(in_r1), .en(WE_1), .clk(CLK), .Q(out_r1));  // open: clr
  Register #(.width(32)) register_1 (.D(in_r9), .en(WE_9), .clk(CLK), .Q(out_r9));  // open: clr
  Register #(.width(32)) register_2 (.D(in_r17), .en(WE_17), .clk(CLK), .Q(out_r17));  // open: clr
  Register #(.width(32)) register_3 (.D(in_r25), .en(WE_25), .clk(CLK), .Q(out_r25));  // open: clr
  Multiplexer #(.select(5), .width(32)) multiplexer_1 (
    .in0({32{1'b0}}), .in1(out_r1), .in2(out_r2), .in3(out_r3), .in4(out_r4), .in5(out_r5), .in6(out_r6),
    .in7(out_r7), .in8(out_r8), .in9(out_r9), .in10(out_r10), .in11(out_r11), .in12(out_r12), .in13(out_r13),
    .in14(out_r14), .in15(out_r15), .in16(out_r16), .in17(out_r17), .in18(out_r18), .in19(out_r19),
    .in20(out_r20), .in21(out_r21), .in22(out_r22), .in23(out_r23), .in24(out_r24), .in25(out_r25),
    .in26(out_r26), .in27(out_r27), .in28(out_r28), .in29(out_r29), .in30(out_r30), .in31(out_r31),
    .out(rs1_data), .sel({1'b0, rs1}));
  Register #(.width(32)) register_4 (.D(in_r2), .en(WE_2), .clk(CLK), .Q(out_r2));  // open: clr
  Register #(.width(32)) register_5 (.D(in_r10), .en(WE_10), .clk(CLK), .Q(out_r10));  // open: clr
  Register #(.width(32)) register_6 (.D(in_r18), .en(WE_18), .clk(CLK), .Q(out_r18));  // open: clr
  Register #(.width(32)) register_7 (.D(in_r26), .en(WE_26), .clk(CLK), .Q(out_r26));  // open: clr
  Register #(.width(32)) register_8 (.D(in_r3), .en(WE_3), .clk(CLK), .Q(out_r3));  // open: clr
  Register #(.width(32)) register_9 (.D(in_r11), .en(WE_11), .clk(CLK), .Q(out_r11));  // open: clr
  Register #(.width(32)) register_10 (.D(in_r19), .en(WE_19), .clk(CLK), .Q(out_r19));  // open: clr
  Register #(.width(32)) register_11 (.D(in_r27), .en(WE_27), .clk(CLK), .Q(out_r27));  // open: clr
  Multiplexer #(.select(5), .width(32)) multiplexer_2 (
    .in0({32{1'b0}}), .in1(out_r1), .in2(out_r2), .in3(out_r3), .in4(out_r4), .in5(out_r5), .in6(out_r6),
    .in7(out_r7), .in8(out_r8), .in9(out_r9), .in10(out_r10), .in11(out_r11), .in12(out_r12), .in13(out_r13),
    .in14(out_r14), .in15(out_r15), .in16(out_r16), .in17(out_r17), .in18(out_r18), .in19(out_r19),
    .in20(out_r20), .in21(out_r21), .in22(out_r22), .in23(out_r23), .in24(out_r24), .in25(out_r25),
    .in26(out_r26), .in27(out_r27), .in28(out_r28), .in29(out_r29), .in30(out_r30), .in31(out_r31),
    .out(rs2_data), .sel({1'b0, rs2}));
  Register #(.width(32)) register_12 (.D(in_r4), .en(WE_4), .clk(CLK), .Q(out_r4));  // open: clr
  Register #(.width(32)) register_13 (.D(in_r12), .en(WE_12), .clk(CLK), .Q(out_r12));  // open: clr
  Register #(.width(32)) register_14 (.D(in_r20), .en(WE_20), .clk(CLK), .Q(out_r20));  // open: clr
  Register #(.width(32)) register_15 (.D(in_r28), .en(WE_28), .clk(CLK), .Q(out_r28));  // open: clr
  Demultiplexer #(.enable("true"), .select(5), .width(32)) demultiplexer_1 (
    .out1(in_r1), .out2(in_r2), .out3(in_r3), .out4(in_r4), .out5(in_r5), .out6(in_r6), .out7(in_r7),
    .out8(in_r8), .out9(in_r9), .out10(in_r10), .out11(in_r11), .out12(in_r12), .out13(in_r13),
    .out14(in_r14), .out15(in_r15), .out16(in_r16), .out17(in_r17), .out18(in_r18), .out19(in_r19),
    .out20(in_r20), .out21(in_r21), .out22(in_r22), .out23(in_r23), .out24(in_r24), .out25(in_r25),
    .out26(in_r26), .out27(in_r27), .out28(in_r28), .out29(in_r29), .out30(in_r30), .out31(in_r31),
    .in(REG_W_DATA), .sel({1'b0, rd}), .en(WRITE_EN));  // open: out0
  Register #(.width(32)) register_16 (.D(in_r5), .en(WE_5), .clk(CLK), .Q(out_r5));  // open: clr
  Register #(.width(32)) register_17 (.D(in_r13), .en(WE_13), .clk(CLK), .Q(out_r13));  // open: clr
  Register #(.width(32)) register_18 (.D(in_r21), .en(WE_21), .clk(CLK), .Q(out_r21));  // open: clr
  Register #(.width(32)) register_19 (.D(in_r29), .en(WE_29), .clk(CLK), .Q(out_r29));  // open: clr
  Register #(.width(32)) register_20 (.D(in_r6), .en(WE_6), .clk(CLK), .Q(out_r6));  // open: clr
  Register #(.width(32)) register_21 (.D(in_r14), .en(WE_14), .clk(CLK), .Q(out_r14));  // open: clr
  Register #(.width(32)) register_22 (.D(in_r22), .en(WE_22), .clk(CLK), .Q(out_r22));  // open: clr
  Register #(.width(32)) register_23 (.D(in_r30), .en(WE_30), .clk(CLK), .Q(out_r30));  // open: clr
  Decoder #(.select(5)) decoder_1 (
    .out1(WE_1), .out2(WE_2), .out3(WE_3), .out4(WE_4), .out5(WE_5), .out6(WE_6), .out7(WE_7), .out8(WE_8),
    .out9(WE_9), .out10(WE_10), .out11(WE_11), .out12(WE_12), .out13(WE_13), .out14(WE_14), .out15(WE_15),
    .out16(WE_16), .out17(WE_17), .out18(WE_18), .out19(WE_19), .out20(WE_20), .out21(WE_21), .out22(WE_22),
    .out23(WE_23), .out24(WE_24), .out25(WE_25), .out26(WE_26), .out27(WE_27), .out28(WE_28), .out29(WE_29),
    .out30(WE_30), .out31(WE_31), .sel({1'b0, rd}), .en(WRITE_EN));  // open: out0
  Register #(.width(32)) register_24 (.D(in_r7), .en(WE_7), .clk(CLK), .Q(out_r7));  // open: clr
  Register #(.width(32)) register_25 (.D(in_r15), .en(WE_15), .clk(CLK), .Q(out_r15));  // open: clr
  Register #(.width(32)) register_26 (.D(in_r23), .en(WE_23), .clk(CLK), .Q(out_r23));  // open: clr
  Register #(.width(32)) register_27 (.D(in_r31), .en(WE_31), .clk(CLK), .Q(out_r31));  // open: clr
  Register #(.width(32)) register_28 (.D(in_r8), .en(WE_8), .clk(CLK), .Q(out_r8));  // open: clr
  Register #(.width(32)) register_29 (.D(in_r16), .en(WE_16), .clk(CLK), .Q(out_r16));  // open: clr
  Register #(.width(32)) register_30 (.D(in_r24), .en(WE_24), .clk(CLK), .Q(out_r24));  // open: clr

  // Other names for the same wires on the sheet: reg1[3:0] = rs1; reg1_data[31:0] = rs1_data; reg2[3:0] = rs2;
  //   reg2_data[31:0] = rs2_data; reg_write[3:0] = rd; reg_write_data[31:0] = REG_W_DATA; WE = WRITE_EN

  // Notes on the sheet:
  //   Outputs
  //   I/O
  //   Inputs
  //   Register Reading
  //   Register Writing
endmodule

module ALU (
  input  [31:0] ALU_X,
  input  [31:0] ALU_Y,
  input  [3:0] ALU_OP,
  output [31:0] ALU_RESULT,
  output ALU_IS_EQ,
  output ALU_IS_GT
);

  wire comparator_1_lt;
  wire [31:0] o_add, o_and, o_div, o_mul, o_mulh, o_or, o_rem, o_sll, o_slt, o_srl, o_sub, o_xor;

  Multiplexer #(.select(4), .width(32)) multiplexer_1 (
    .in0(o_add), .in1(o_sub), .in2(o_and), .in3(o_or), .in4(o_xor), .in5(o_sll), .in6(o_srl), .in7(o_mul),
    .in8(o_mulh), .in9(o_div), .in10(o_rem), .in11(o_slt), .out(ALU_RESULT), .sel(ALU_OP));  // open: in12, in13, in14, in15
  Adder #(.width(32)) adder_1 (.a(ALU_X), .b(ALU_Y), .out(o_add));  // open: cin, cout
  Subtractor #(.width(32)) subtractor_1 (.a(ALU_X), .b(ALU_Y), .out(o_sub));  // open: bin, bout
  assign o_and = ALU_X & ALU_Y;  // AND_Gate and_1, 32 bits wide
  assign o_or = ALU_X | ALU_Y;  // OR_Gate or_1, 32 bits wide
  assign o_xor = ALU_X ^ ALU_Y;  // XOR_Gate xor_1, 32 bits wide
  Shifter #(.width(32)) shifter_1 (.in(ALU_X), .\dist (ALU_Y[4:0]), .out(o_sll));
  Comparator #(.width(32)) comparator_1 (.a(ALU_X), .b(ALU_Y), .lt(comparator_1_lt));  // open: gt, eq
  Shifter #(.shift("lr"), .width(32)) shifter_2 (.in(ALU_X), .\dist (ALU_Y[4:0]), .out(o_srl));
  Multiplier #(.width(32)) multiplier_1 (.a(ALU_X), .b(ALU_Y), .out(o_mul));  // open: cin, cout
  Multiplier #(.width(32)) multiplier_2 (.a(ALU_X), .b(ALU_Y), .cout(o_mulh));  // open: out, cin
  Divider #(.width(32)) divider_1 (.a(ALU_X), .b(ALU_Y), .out(o_div));  // open: upper, rem
  Divider #(.width(32)) divider_2 (.a(ALU_X), .b(ALU_Y), .rem(o_rem));  // open: out, upper
  Comparator #(.width(32)) comparator_2 (.a(ALU_X), .b(ALU_Y), .gt(ALU_IS_GT), .eq(ALU_IS_EQ));  // open: lt
  Bit_Extender #(.in_width(1), .out_width(32)) bit_extender_1 (.out(o_slt));  // open: in

  // Other names for the same wires on the sheet: isEqual = ALU_IS_EQ; isGreater = ALU_IS_GT; OP[3:0] = ALU_OP;
  //   result[31:0] = ALU_RESULT; X[31:0] = ALU_X; Y[31:0] = ALU_Y

  // Notes on the sheet:
  //   Outputs
  //   I/O
  //   Operation Selection
  //   Inputs
  //   Operations
endmodule
